# Fritzing sketch Bluefruit_Diagram (saved by Fritzing 0.9.10b)

parts:
  Part1 = Adafruit FTDI Friend [part_number="Adafruit #284"]
  Part2 = Adafruit Bluefruit LE UART Friend [part_number="Adafruit #2479"]

nets:
  GND: Part1.GND, Part2.GND
  N1: Part1.CTS, Part2.RTS
  VCC: Part1.VCC, Part2.VIN
  N2: Part1.TX, Part2.RXI
  N3: Part1.RX, Part2.TXO
  N4: Part1.RTS/DTR, Part2.CTS

notes:
  Wire colors match FTDI Cable colors, in case you choose to use a Genuine FTDI Cable.
  Make sure the switch is in the CMD position.

custom parts:
  Adafruit FTDI Friend: Long gone are the days of parallel ports and serial ports. Now the USB port reigns supreme! But USB is hard, and you just want to transfer your every-day serial data from a microcontroller to computer. What now? Enter the FTDI Friend! The FTDI Friend is a tweaked out FTDI FT232RL chip adapter. Sure, like the well-known FTDI cable, it can provide power to your project and there are 4 signal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
  Adafruit Bluefruit LE UART Friend: The Bluefruit LE UART Friend makes it easy to add Bluetooth Low Energy connectivity to anything with a hardware or software serial port. We even have nice hardware flow control so you won't have to think about losing data. Connect to your Arduino or other microcontroller or even just a standard FTDI cable for debugging and testing.
